// Logisim project s-mips.circ as structural Verilog: 14 circuits, main circuit S-MIPS Board
module S_MIPS_Board (
  input  DESHABILITAR_DISPATCHER,
  output halt
);

  wire button_1_out, CLK, CS, d_ff_1_q, LCLR, LoadRAM, LoadRAMOn, LW, R_R_W, R_W, ram_dispatcher_1_finished,
       RCS, Reset_out, RST, TTY_EN;
  wire [2:0] KDB;
  wire [3:0] LMask, Mask, ram_1_read_time, ram_1_write_time, RMask;
  wire [6:0] KDB_DATA, TTY_DATA;
  wire [15:0] Addr, LAddr, RAddr;
  wire [31:0] I0, I1, I2, I3, LData, ram_1_data_out_0, ram_1_data_out_1, ram_1_data_out_2, ram_1_data_out_3,
       RI0, RI1, RI2, RI3;

  TTY #(.rows(25), .cols(80)) tty_1 (.data(TTY_DATA), .clk(CLK), .we(TTY_EN), .clr(RST));
  not not_1 (LoadRAMOn, ram_dispatcher_1_finished);
  RAM_Dispatcher ram_dispatcher_1 (
    .WriteTime(ram_1_write_time), .Clock(CLK), .Data(LData), .Address(LAddr), .Mask(LMask),
    .Finished(ram_dispatcher_1_finished), .Write(LW), .CLR(LCLR));
  Keyboard #(.buflen(64)) keyboard_1 (.clk(CLK), .re(KDB[0]), .avail(KDB[2]), .data(KDB_DATA));  // open: clr
  RAM ram_1 (
    .Address(RAddr), .Data_Out_0(ram_1_data_out_0), .Data_Out_1(ram_1_data_out_1),
    .Data_Out_2(ram_1_data_out_2), .Data_Out_3(ram_1_data_out_3), .Data_In_0(RI0), .Data_In_1(RI1),
    .Data_In_2(RI2), .Data_In_3(RI3), .Mask(RMask), .nRead_Write(R_R_W), .Chip_Select(RCS),
    .Read_Time(ram_1_read_time), .Reset(button_1_out), .Write_Time(ram_1_write_time));
  Button button_1 (.out(button_1_out));
  D_Flip_Flop d_ff_1 (.clk(CLK), .D(1'b1), .Q(d_ff_1_q), .reset(Reset_out));  // open: Qn, preset, en
  Button Reset (.out(Reset_out));
  S_MIPS s_mips_1 (
    .Kbd_Enable(KDB[0]), .Address(Addr), .Kbd_Clear(KDB[1]), .Kbd_Available(KDB[2]), .RAM_In_0(I0),
    .Kbd_ASCII_Data(KDB_DATA), .RAM_In_1(I1), .TTY_Enable(TTY_EN), .RAM_In_2(I2), .RAM_In_3(I3),
    .TTY_ASCII_Data(TTY_DATA), .Reset(RST), .RAM_Out_0(ram_1_data_out_0), .Clock(CLK),
    .RAM_Out_1(ram_1_data_out_1), .Stop(halt), .RAM_Out_2(ram_1_data_out_2), .RAM_Out_3(ram_1_data_out_3),
    .Mask(Mask), .Read_Time(ram_1_read_time), .Write_Time(ram_1_write_time), .nRead_Write(R_W),
    .Chip_Select(CS));
  D_Flip_Flop d_ff_2 (.clk(CLK), .D(d_ff_1_q), .Qn(LCLR), .reset(Reset_out));  // open: Q, preset, en
  or or_1 (RST, LCLR, LoadRAM);
  Clock clock_1 (.out(CLK));
  Multiplexer #(.width(32), .enable("false")) multiplexer_1 (.in0(I0), .in1(LData), .out(RI0), .sel(LoadRAM));
  Multiplexer #(.width(32), .enable("false")) multiplexer_2 (.in0(I1), .in1(LData), .out(RI1), .sel(LoadRAM));
  Multiplexer #(.width(32), .enable("false")) multiplexer_3 (.in0(I2), .in1(LData), .out(RI2), .sel(LoadRAM));
  Multiplexer #(.width(32), .enable("false")) multiplexer_4 (.in0(I3), .in1(LData), .out(RI3), .sel(LoadRAM));
  and and_1 (LoadRAM, ~DESHABILITAR_DISPATCHER, LoadRAMOn);  // AND_Gate
  Multiplexer #(.width(16), .enable("false")) multiplexer_5 (.in0(Addr), .in1(LAddr), .out(RAddr), .sel(LoadRAM));
  Multiplexer #(.width(4), .enable("false")) multiplexer_6 (.in0(Mask), .in1(LMask), .out(RMask), .sel(LoadRAM));
  Multiplexer #(.enable("false")) multiplexer_7 (.in0(CS), .in1(LW), .out(RCS), .sel(LoadRAM));
  Multiplexer #(.enable("false")) multiplexer_8 (.in0(R_W), .in1(LW), .out(R_R_W), .sel(LoadRAM));

  // Notes on the sheet:
  //   NO MODIFICAR
  //   Keyboard
endmodule

module RAM (
  input  [15:0] Address,
  input  [31:0] Data_In_0,
  input  [31:0] Data_In_1,
  input  [31:0] Data_In_2,
  input  [31:0] Data_In_3,
  input  [3:0] Mask,
  input  nRead_Write,
  input  Chip_Select,
  input  Reset,
  output [31:0] Data_Out_0,
  output [31:0] Data_Out_1,
  output [31:0] Data_Out_2,
  output [31:0] Data_Out_3,
  output [3:0] Read_Time,
  output [3:0] Write_Time
);

  wire and_2_out, and_3_out, and_4_out, and_5_out, and_6_out, and_7_out, and_8_out, and_9_out, Changed, CLK,
       comparator_2_eq, comparator_3_eq, comparator_4_eq, comparator_5_eq, comparator_6_eq, Count,
       demultiplexer_3_out0, Idle, Idle_q, Load, Load0, Load1, nand_1_out, or_1_out, or_2_out, or_3_out,
       or_4_out, or_5_out, or_6_out, or_7_out, or_8_out, or_9_out, or_10_out, Proc_q, Update_Mem, Zero_Time;
  wire [3:0] counter_1_q, multiplexer_1_out, subtractor_1_out;
  wire [31:0] register_1_q, register_2_q, register_3_q, register_4_q, register_5_q;

  // Probe on 4'b0011
  // Probe on 4'b0010
  Multiplexer #(.width(4), .enable("false")) multiplexer_1 (
    .in0(4'b0011), .in1(4'b0010), .out(multiplexer_1_out), .sel(nRead_Write));
  or or_1 (or_1_out, Idle, Update_Mem);
  or or_2 (or_2_out, ~Chip_Select, Reset);  // OR_Gate
  Subtractor #(.width(4)) subtractor_1 (.a(multiplexer_1_out), .b(4'b0010), .out(subtractor_1_out));  // open: bin, bout
  D_Flip_Flop u_Idle (.clk(CLK), .D(or_1_out), .Q(Idle_q), .preset(or_2_out));  // open: Qn, en, reset
  Demultiplexer #(.enable("false")) demultiplexer_1 (.out0(Idle), .out1(Load0), .in(Idle_q), .sel(Changed));
  // Probe on counter_1_q
  Counter #(.width(4), .max('hf)) counter_1 (
    .load(Load), .D(subtractor_1_out), .count(Count), .Q(counter_1_q), .clk(CLK), .clr(or_3_out));  // open: carry
  or or_3 (or_3_out, ~Chip_Select, Reset);  // OR_Gate
  Comparator #(.width(4), .mode("unsigned")) comparator_1 (
    .a(4'b0000), .b(counter_1_q), .eq(Zero_Time));  // open: gt, lt
  or or_4 (or_4_out, Count, Load0, Load1);
  Register #(.width(32)) register_1 (.D(Data_In_0), .en(Chip_Select), .Q(register_1_q), .clk(CLK), .clr(or_5_out));
  or or_5 (or_5_out, ~Chip_Select, Reset);  // OR_Gate
  Register #(.width(32)) register_2 (.D(Data_In_1), .en(Chip_Select), .Q(register_2_q), .clk(CLK), .clr(or_6_out));
  or or_6 (or_6_out, ~Chip_Select, Reset);  // OR_Gate
  Register #(.width(32)) register_3 (.D(Data_In_2), .en(Chip_Select), .Q(register_3_q), .clk(CLK), .clr(or_7_out));
  or or_7 (or_7_out, ~Chip_Select, Reset);  // OR_Gate
  Register #(.width(32)) register_4 (.D(Data_In_3), .en(Chip_Select), .Q(register_4_q), .clk(CLK), .clr(or_8_out));
  or or_8 (or_8_out, ~Chip_Select, Reset);  // OR_Gate
  Register #(.width(32)) register_5 (
    .D({{11{1'b1}}, nRead_Write, Mask, Address}), .en(Chip_Select), .Q(register_5_q), .clk(CLK),
    .clr(or_9_out));
  or or_9 (or_9_out, ~Chip_Select, Reset);  // OR_Gate
  D_Flip_Flop Proc (.clk(CLK), .D(or_4_out), .Q(Proc_q), .reset(or_10_out));  // open: Qn, preset, en
  or or_10 (or_10_out, ~Chip_Select, Reset);  // OR_Gate
  Demultiplexer #(.enable("false")) demultiplexer_2 (
    .out0(Count), .out1(Update_Mem), .in(demultiplexer_3_out0), .sel(Zero_Time));
  Demultiplexer #(.enable("false")) demultiplexer_3 (
    .out0(demultiplexer_3_out0), .out1(Load1), .in(Proc_q), .sel(Changed));
  Clock clock_1 (.out(CLK));
  Comparator #(.width(32)) comparator_2 (.a(register_1_q), .b(Data_In_0), .eq(comparator_2_eq));  // open: gt, lt
  Comparator #(.width(32)) comparator_3 (.a(register_2_q), .b(Data_In_1), .eq(comparator_3_eq));  // open: gt, lt
  Comparator #(.width(32)) comparator_4 (.a(register_3_q), .b(Data_In_2), .eq(comparator_4_eq));  // open: gt, lt
  Comparator #(.width(32)) comparator_5 (.a(register_4_q), .b(Data_In_3), .eq(comparator_5_eq));  // open: gt, lt
  Comparator #(.width(32)) comparator_6 (
    .a(register_5_q), .b({{11{1'b1}}, nRead_Write, Mask, Address}), .eq(comparator_6_eq));  // open: gt, lt
  nand nand_1 (nand_1_out, comparator_6_eq, comparator_2_eq, comparator_3_eq, comparator_4_eq, comparator_5_eq);
  and and_1 (Changed, nand_1_out, Chip_Select);
  or or_11 (Load, Count, Load1, Load0);
  and and_2 (and_2_out, Mask[0], Update_Mem, nRead_Write);
  and and_3 (and_3_out, Mask[1], Update_Mem, nRead_Write);
  and and_4 (and_4_out, Mask[2], Update_Mem, nRead_Write);
  and and_5 (and_5_out, Mask[3], Update_Mem, nRead_Write);
  RAM_part #(.addrWidth(16), .dataWidth(32), .bus("separate")) ram_1 (
    .addr(Address), .din(Data_In_0), .data(Data_Out_0), .str(and_2_out), .sel(Chip_Select), .clk(CLK),
    .ld(and_6_out), .clr(Reset));
  and and_6 (and_6_out, ~nRead_Write, Idle);  // AND_Gate
  RAM_part #(.addrWidth(16), .dataWidth(32), .bus("separate")) ram_2 (
    .addr(Address), .din(Data_In_1), .data(Data_Out_1), .str(and_3_out), .sel(Chip_Select), .clk(CLK),
    .ld(and_7_out), .clr(Reset));
  and and_7 (and_7_out, ~nRead_Write, Idle);  // AND_Gate
  RAM_part #(.addrWidth(16), .dataWidth(32), .bus("separate")) ram_3 (
    .addr(Address), .din(Data_In_2), .data(Data_Out_2), .str(and_4_out), .sel(Chip_Select), .clk(CLK),
    .ld(and_8_out), .clr(Reset));
  and and_8 (and_8_out, ~nRead_Write, Idle);  // AND_Gate
  RAM_part #(.addrWidth(16), .dataWidth(32), .bus("separate")) ram_4 (
    .addr(Address), .din(Data_In_3), .data(Data_Out_3), .str(and_5_out), .sel(Chip_Select), .clk(CLK),
    .ld(and_9_out), .clr(Reset));
  and and_9 (and_9_out, ~nRead_Write, Idle);  // AND_Gate

  assign Read_Time = 4'b0011;
  assign Write_Time = 4'b0010;

  // Other names for the same wires on the sheet: M0 = Mask[0]; M1 = Mask[1]; M2 = Mask[2]; M3 = Mask[3];
  //   RW = nRead_Write; CLR = Reset; CS = Chip_Select; Load2 = Count

  // Notes on the sheet:
  //   NO MODIFICAR
  //   excepto quizás los valores RT y WT
  //   BANK0
  //   BANK1
  //   BANK2
  //   BANK3
endmodule

module S_MIPS (
  input  Kbd_Available,
  input  [6:0] Kbd_ASCII_Data,
  input  [31:0] RAM_Out_0,
  input  [31:0] RAM_Out_1,
  input  Reset,
  input  [31:0] RAM_Out_2,
  input  Clock,
  input  [31:0] RAM_Out_3,
  input  [3:0] Read_Time,
  input  [3:0] Write_Time,
  output Kbd_Enable,
  output [15:0] Address,
  output Kbd_Clear,
  output TTY_Enable,
  output [6:0] TTY_ASCII_Data,
  output Stop,
  output [31:0] RAM_In_0,
  output [31:0] RAM_In_1,
  output [31:0] RAM_In_2,
  output [31:0] RAM_In_3,
  output [3:0] Mask,
  output nRead_Write,
  output Chip_Select
);

  wire and_1_out, control_unit_1_comparation, control_unit_1_hi_lo_en, control_unit_1_hi_lo_selector,
       control_unit_1_inmediate, control_unit_1_load_instruction, control_unit_1_load_pc,
       control_unit_1_pop_push, control_unit_1_ram_op, control_unit_1_read_write, control_unit_1_register_op,
       control_unit_1_rnd, control_unit_1_sp_en, control_unit_1_stack_op, control_unit_1_unsigned, KBD,
       not_1_out, not_2_out;
  wire [1:0] Offset;
  wire [2:0] control_unit_1_alu_op, control_unit_1_branch_op;
  wire [5:0] Func_code, OP_code;
  wire [6:0] multiplexer_1_out;
  wire [31:0] RAM_INPUT;

  not not_1 (not_1_out, Reset);
  and and_1 (and_1_out, KBD, Kbd_Available);
  Control_Unit control_unit_1 (
    .OP_code(OP_code), .Func_code(Func_code), .Write_Time(Write_Time), .Read_Time(Read_Time),
    .Start(not_1_out), .CLK(Clock), .RST(Reset), .ALU_Op(control_unit_1_alu_op),
    .Branch_Op(control_unit_1_branch_op), .Inmediate(control_unit_1_inmediate),
    .Unsigned(control_unit_1_unsigned), .Comparation(control_unit_1_comparation),
    .Hi_Lo_EN(control_unit_1_hi_lo_en), .Register_Op(control_unit_1_register_op),
    .Hi_Lo_Selector(control_unit_1_hi_lo_selector), .RAM_op(control_unit_1_ram_op),
    .Stack_op(control_unit_1_stack_op), .pop_push(control_unit_1_pop_push), .SP_En(control_unit_1_sp_en),
    .RND(control_unit_1_rnd), .KBD_Sel(KBD), .Chip_selector(Chip_Select),
    .Load_Instruction(control_unit_1_load_instruction), .Read_Write(control_unit_1_read_write),
    .Load_PC(control_unit_1_load_pc), .RAM_RW(nRead_Write), .TTY(TTY_Enable), .KBD_ENABLE(Kbd_Enable),
    .END(Stop));
  Demultiplexer #(.select(2), .width(32)) demultiplexer_1 (
    .out0(RAM_In_0), .out1(RAM_In_1), .out2(RAM_In_2), .out3(RAM_In_3), .in(RAM_INPUT), .sel(Offset));  // open: en
  Decoder_part #(.select(2)) decoder_1 (
    .out0(Mask[0]), .out1(Mask[1]), .out2(Mask[2]), .out3(Mask[3]), .sel(Offset));  // open: en
  not not_2 (not_2_out, Clock);
  Multiplexer #(.width(7)) multiplexer_1 (
    .in0({7{1'b1}}), .in1(Kbd_ASCII_Data), .out(multiplexer_1_out), .sel(and_1_out));  // open: en
  Data_Path data_path_1 (
    .Bank_1(RAM_Out_0), .Bank_2(RAM_Out_1), .Bank_3(RAM_Out_2), .Bank_4(RAM_Out_3),
    .KBD_Input(multiplexer_1_out), .Alu_OP(control_unit_1_alu_op), .Branch_OP(control_unit_1_branch_op),
    .Inmediate(control_unit_1_inmediate), .Unsigned(control_unit_1_unsigned),
    .Comparation(control_unit_1_comparation), .Hi_Lo_OP(control_unit_1_hi_lo_en),
    .Reg_Op(control_unit_1_register_op), .Hi_Lo_Selector(control_unit_1_hi_lo_selector),
    .RAM_Op(control_unit_1_ram_op), .Stack_Op(control_unit_1_stack_op), .pop_push(control_unit_1_pop_push),
    .SP_En(control_unit_1_sp_en), .RND(control_unit_1_rnd), .KBD_sel(KBD),
    .Load_Inst(control_unit_1_load_instruction), .R_W(control_unit_1_read_write),
    .Load_PC(control_unit_1_load_pc), .RST(Reset), .CLK(not_2_out), .OP_code(OP_code), .Func_code(Func_code),
    .Address(Address), .RAM_Output(RAM_INPUT), .Offset(Offset), .TTY(TTY_ASCII_Data));

  assign Kbd_Clear = Reset;

  // Other names for the same wires on the sheet: CLK = Clock; CS = Chip_Select; KBD_AVAIL = Kbd_Available;
  //   CLR = Reset; KBD_CLR = Reset; KBD_DATA[6:0] = Kbd_ASCII_Data; RAM_A[15:0] = Address;
  //   RAM_INPUT_0[31:0] = RAM_In_0; RAM_INPUT_1[31:0] = RAM_In_1; RAM_INPUT_2[31:0] = RAM_In_2;
  //   RAM_INPUT_3[31:0] = RAM_In_3; RAM_MASK[3:0] = Mask; RAM_OUTPUT_0[31:0] = RAM_Out_0;
  //   RAM_OUTPUT_1[31:0] = RAM_Out_1; RAM_OUTPUT_2[31:0] = RAM_Out_2; RAM_OUTPUT_3[31:0] = RAM_Out_3;
  //   RW = nRead_Write; TTY_DATA[6:0] = TTY_ASCII_Data

  // Notes on the sheet:
  //   RAM ADDRESS
  //   DATA FROM RAM
  //   DATA TO RAM
  //   DATA WRITE MASK
  //   RAM TIMING
  //   RAM CONTROL
  //   KEYBOARD
  //   TTY
  //   SEQUENCING
endmodule

module RAM_Dispatcher (
  input  [3:0] WriteTime,
  input  Clock,
  input  CLR,
  output [31:0] Data,
  output [15:0] Address,
  output [3:0] Mask,
  output Finished,
  output Write
);

  wire demultiplexer_2_out1, demultiplexer_3_out1, End, IDLE_q, IncAddr, Load, or_1_out, or_2_out, While_q,
       WriteEnd;
  wire [3:0] counter_1_q;
  wire [31:0] CurrentAddress_q;

  Counter #(.width(32), .max('hffffffff)) CurrentAddress (
    .count(IncAddr), .Q({CurrentAddress_q[31:18], Address, CurrentAddress_q[1:0]}), .clk(Clock), .clr(CLR));  // open: load, D, carry
  or or_1 (or_1_out, IncAddr, demultiplexer_3_out1, Finished);
  D_Flip_Flop IDLE (.clk(Clock), .D(or_1_out), .Q(IDLE_q), .preset(CLR));  // open: Qn, en, reset
  Demultiplexer #(.enable("false")) demultiplexer_1 (.out0(Load), .out1(Finished), .in(IDLE_q), .sel(End));
  D_Flip_Flop While (.clk(Clock), .D(or_2_out), .Q(While_q), .reset(CLR));  // open: Qn, preset, en
  or or_2 (or_2_out, Write, Load);
  RAM_part #(.addrWidth(18), .dataWidth(32)) ram_1 (
    .addr({Address, CurrentAddress_q[1:0]}), .data(Data), .clk(Clock));  // open: sel, ld, clr
  Demultiplexer #(.enable("false")) demultiplexer_2 (
    .out0(Write), .out1(demultiplexer_2_out1), .in(While_q), .sel(WriteEnd));
  Decoder_part #(.select(2)) decoder_1 (
    .out0(Mask[0]), .out1(Mask[1]), .out2(Mask[2]), .out3(Mask[3]), .sel(CurrentAddress_q[1:0]));  // open: en
  Demultiplexer #(.enable("false")) demultiplexer_3 (
    .out0(IncAddr), .out1(demultiplexer_3_out1), .in(demultiplexer_2_out1), .sel(End));
  Counter #(.width(4), .max('hf)) counter_1 (
    .load(Load), .D(WriteTime), .count(Write), .Q(counter_1_q), .clk(Clock));  // open: carry, clr
  Comparator #(.width(32)) comparator_1 (.a(Data), .b({32{1'b1}}), .eq(End));  // open: gt, lt
  Comparator #(.width(4)) comparator_2 (.a(4'b0000), .b(counter_1_q), .eq(WriteEnd));  // open: gt, lt

  // Other names for the same wires on the sheet: CLK = Clock; Count = Write; WT[3:0] = WriteTime
endmodule

module Data_Path (
  input  [31:0] Bank_1,
  input  [31:0] Bank_2,
  input  [31:0] Bank_3,
  input  [31:0] Bank_4,
  input  [6:0] KBD_Input,
  input  [2:0] Alu_OP,
  input  [2:0] Branch_OP,
  input  Inmediate,
  input  Unsigned,
  input  Comparation,
  input  Hi_Lo_OP,
  input  Reg_Op,
  input  Hi_Lo_Selector,
  input  RAM_Op,
  input  Stack_Op,
  input  pop_push,
  input  SP_En,
  input  RND,
  input  KBD_sel,
  input  Load_Inst,
  input  R_W,
  input  Load_PC,
  input  CLK,
  input  RST,
  output [5:0] OP_code,
  output [5:0] Func_code,
  output [15:0] Address,
  output [31:0] RAM_Output,
  output [1:0] Offset,
  output [6:0] TTY
);

  wire A___B, A___B_t, A___B_t_t, and_1_out, or_1_out, or_2_out;
  wire [2:0] priority_encoder_1_out;
  wire [4:0] A_Select, B_Select, Dest_Address, multiplexer_2_out, x;
  wire [15:0] k;
  wire [25:0] Jump_Dest;
  wire [31:0] A, B, bit_extender_1_out, bit_extender_2_out, bit_extender_3_out, Data_Input, Hi, High_res,
       Instruction, Lo, multiplexer_1_out, multiplexer_3_out, multiplexer_6_out, Next_PC, PC, random_1_out,
       result, SP;

  assign bit_extender_1_out = {{16{k[15]}}, k};  // Bit_Extender bit_extender_1
  or or_1 (or_1_out, Inmediate, RAM_Op);
  Instruction_Decoder instruction_decoder_1 (
    .instruccion(Instruction), .Load(Load_Inst), .CLK(CLK), .RST(RST), .OP_code(OP_code), .x(x),
    .Func_code(Func_code), .Rs(A_Select), .Rt(B_Select), .dest(Jump_Dest), .k(k), .Rd(Dest_Address));
  Multiplexer #(.width(32)) multiplexer_1 (
    .in0(B), .in1(bit_extender_1_out), .out(multiplexer_1_out), .sel(Inmediate));  // open: en
  Multiplexer #(.width(5)) multiplexer_2 (
    .in0(Dest_Address), .in1(B_Select), .out(multiplexer_2_out), .sel(or_1_out));  // open: en
  Program_Counter program_counter_1 (.Input(Next_PC), .EN(Load_PC), .Output(PC), .Clock(CLK), .Reset(RST));
  Branch_Control branch_control_1 (
    .PC_Before(PC), .IA(Jump_Dest), .Rs(A), .Rs______Rt(A___B_t), .PC_After(Next_PC), .k(k),
    .Instruction(Branch_OP));
  ALU alu_1 (
    .A(A), .B(multiplexer_1_out), .Unsigned(Unsigned), .Selector(Alu_OP), .Result(result),
    .To_High(High_res), .Greater_Out(A___B_t_t), .Equal_Out(A___B_t), .Lesser_Out(A___B));
  and and_1 (and_1_out, R_W, ~Hi_Lo_OP);  // AND_Gate
  Register_File register_file_1 (
    .HighO(Hi), .SP(SP), .LowO(Lo), .SA(A_Select), .SB(B_Select), .DI(Data_Input), .HighI(High_res),
    .LowI(result), .Clock(CLK), .Reset(RST), .pop_push(pop_push), .Stack(SP_En), .RW(and_1_out),
    .DA(multiplexer_2_out), .HL_En(Hi_Lo_OP), .A(A), .B(B));
  Multiplexer #(.width(32)) multiplexer_3 (
    .in0(Lo), .in1(Hi), .out(multiplexer_3_out), .sel(Hi_Lo_Selector));  // open: en
  assign bit_extender_2_out = {{25{KBD_Input[6]}}, KBD_Input};  // Bit_Extender bit_extender_2
  or or_2 (or_2_out, RAM_Op, Stack_Op);
  Addresser addresser_1 (
    .PC(PC), .Register(A), .Const(k), .SP(SP), .RAM_op(RAM_Op), .Stack_op(Stack_Op), .Offset(Offset),
    .Address(Address));
  assign bit_extender_3_out = {{31{1'b0}}, A___B};  // Bit_Extender bit_extender_3
  Random #(.width(32)) random_1 (.clk(CLK), .out(random_1_out));  // open: next, clr
  Priority_Encoder priority_encoder_1 (
    .in0(1'b1), .in1(or_2_out), .in2(Comparation), .in3(Reg_Op), .in4(RND), .in5(KBD_sel),
    .out(priority_encoder_1_out));  // open: in6, in7, en_in, gs, en_out
  Multiplexer #(.select(2), .width(32)) multiplexer_4 (
    .in0(Bank_1), .in1(Bank_2), .in2(Bank_3), .in3(Bank_4), .out(Instruction), .sel(Offset));  // open: en
  Multiplexer #(.select(3), .width(32)) multiplexer_5 (
    .in0(result), .in1(Instruction), .in2(bit_extender_3_out), .in3(multiplexer_3_out), .in4(random_1_out),
    .in5(bit_extender_2_out), .out(Data_Input), .sel(priority_encoder_1_out));  // open: in6, in7, en
  Multiplexer #(.width(32)) multiplexer_6 (.in0(B), .in1(A), .out(multiplexer_6_out), .sel(Stack_Op));  // open: en
  Little_Endian little_endian_1 (.in_1(multiplexer_6_out), .Output(RAM_Output));
  Bit_Extender #(.in_width(32), .out_width(7)) bit_extender_4 (.in(A), .out(TTY));

  // Other names for the same wires on the sheet: Inm = Inmediate; KBD = KBD_sel; Reset = RST; Uns = Unsigned
endmodule

module Addresser (
  input  [31:0] PC,
  input  [31:0] Register,
  input  [15:0] Const,
  input  [31:0] SP,
  input  RAM_op,
  input  Stack_op,
  output [1:0] Offset,
  output [15:0] Address
);

  wire [31:0] adder_1_out, bit_extender_1_out, multiplexer_1_out, multiplexer_2_out;

  assign bit_extender_1_out = {{16{1'b0}}, Const};  // Bit_Extender bit_extender_1
  Adder #(.width(32)) adder_1 (.a(Register), .b(bit_extender_1_out), .out(adder_1_out));  // open: cin, cout
  Multiplexer #(.width(32)) multiplexer_1 (
    .in0(PC), .in1(adder_1_out), .out(multiplexer_1_out), .sel(RAM_op));  // open: en
  Multiplexer #(.width(32)) multiplexer_2 (
    .in0(multiplexer_1_out), .in1(SP),
    .out({multiplexer_2_out[31:20], Address, Offset, multiplexer_2_out[1:0]}), .sel(Stack_op));  // open: en

  // Other names for the same wires on the sheet: k[15:0] = Const; Reg[31:0] = Register
endmodule

module ALU (
  input  [31:0] A,
  input  [31:0] B,
  input  [2:0] Selector,
  input  Unsigned,
  output [31:0] Result,
  output [31:0] To_High,
  output Greater_Out,
  output Equal_Out,
  output Lesser_Out
);

  wire comparator_1_lt, comparator_2_lt, comparator_5_eq, eq, eqU, greater, greaterU, less, lessU;
  wire [31:0] \and , div, divu, mult, mulu, negator_1_out, negator_2_out, \nor , \or , rest, resta, restu,
       suma, tunnel, tunnel_t, Uns1, Uns2, X, \xor ;

  Negator #(.width(32)) negator_1 (.in(A), .out(negator_1_out));
  Comparator #(.width(32)) comparator_1 (.a(A), .b({32{1'b0}}), .lt(comparator_1_lt));  // open: gt, eq
  Negator #(.width(32)) negator_2 (.in(B), .out(negator_2_out));
  Comparator #(.width(32)) comparator_2 (.a(B), .b({32{1'b0}}), .lt(comparator_2_lt));  // open: gt, eq
  Multiplexer #(.width(32)) multiplexer_1 (
    .in0(A), .in1(negator_1_out), .out(Uns1), .sel(comparator_1_lt));  // open: en
  Multiplexer #(.width(32)) multiplexer_2 (
    .in0(B), .in1(negator_2_out), .out(Uns2), .sel(comparator_2_lt));  // open: en
  Multiplexer #(.width(32)) multiplexer_3 (.in0(mult), .in1(mulu), .out(X), .sel(Unsigned));  // open: en
  Adder #(.width(32)) adder_1 (.a(A), .b(B), .out(suma));  // open: cin, cout
  Subtractor #(.width(32)) subtractor_1 (.a(A), .b(B), .out(resta));  // open: bin, bout
  Multiplier #(.width(32)) multiplier_1 (.a(A), .b(B), .out(mult));  // open: cin, cout
  Multiplier #(.width(32)) multiplier_2 (.a(Uns1), .b(Uns2), .out(mulu));  // open: cin, cout
  Divider #(.width(32)) divider_1 (.a(A), .b(B), .out(div), .rem(rest));  // open: upper
  Divider #(.width(32)) divider_2 (.a(Uns1), .b(Uns2), .out(divu), .rem(restu));  // open: upper
  Comparator #(.width(32)) comparator_3 (.a(A), .b(B), .gt(greater), .eq(eq), .lt(less));
  Comparator #(.width(32)) comparator_4 (.a(Uns1), .b(Uns2), .gt(greaterU), .eq(eqU), .lt(lessU));
  Multiplexer #(.width(32)) multiplexer_4 (.in0(div), .in1(divu), .out(tunnel_t), .sel(Unsigned));  // open: en
  assign \and  = A & B;  // AND_Gate and_1, 32 bits wide
  assign \or  = A | B;  // OR_Gate or_1, 32 bits wide
  assign \nor  = ~(A | B);  // NOR_Gate nor_1, 32 bits wide
  assign \xor  = A ^ B;  // XOR_Gate xor_1, 32 bits wide
  Multiplexer multiplexer_5 (.in0(greater), .in1(greaterU), .out(Greater_Out), .sel(Unsigned));  // open: en
  Multiplexer multiplexer_6 (.in0(eq), .in1(eqU), .out(Equal_Out), .sel(Unsigned));  // open: en
  Multiplexer multiplexer_7 (.in0(less), .in1(lessU), .out(Lesser_Out), .sel(Unsigned));  // open: en
  Multiplexer #(.width(32)) multiplexer_8 (.in0(rest), .in1(restu), .out(tunnel), .sel(Unsigned));  // open: en
  Multiplexer #(.select(3), .width(32)) multiplexer_9 (
    .in0(suma), .in1(resta), .in2(X), .in3(tunnel_t), .in4(\and ), .in5(\nor ), .in6(\or ), .in7(\xor ),
    .out(Result), .sel(Selector));  // open: en
  Comparator #(.width(3)) comparator_5 (.a(Selector), .b(3'b011), .eq(comparator_5_eq));  // open: gt, lt
  Multiplexer #(.width(32)) multiplexer_10 (
    .in0(Result), .in1(tunnel), .out(To_High), .sel(comparator_5_eq));  // open: en

  // Notes on the sheet:
  //   flags
endmodule

module Instruction_Decoder (
  input  [31:0] instruccion,
  input  Load,
  input  CLK,
  input  RST,
  output [25:0] dest,
  output [15:0] k,
  output [5:0] OP_code,
  output [5:0] Func_code,
  output [4:0] x,
  output [4:0] Rs,
  output [4:0] Rt,
  output [4:0] Rd
);

  Register #(.width(32)) register_1 (.D(instruccion), .en(Load), .Q({OP_code, dest}), .clk(CLK), .clr(RST));

  assign Func_code = dest[5:0];
  assign k = dest[15:0];
  assign Rd = dest[15:11];
  assign Rs = dest[25:21];
  assign Rt = dest[20:16];
  assign x = dest[10:6];

  // Other names for the same wires on the sheet: Inst[31:0] = instruccion; Load_Inst = Load;
  //   New_Inst[31:0] = {OP_code, dest}
endmodule

module Program_Counter (
  input  [31:0] Input,
  input  Clock,
  input  Reset,
  input  EN,
  output [31:0] Output
);

  Register #(.width(32)) register_1 (.D(Input), .en(EN), .Q(Output), .clk(Clock), .clr(Reset));
endmodule

module Branch_Control (
  input  [31:0] PC_Before,
  input  [31:0] Rs,
  input  [15:0] k,
  input  [2:0] Instruction,
  input  Rs______Rt,
  input  [25:0] IA,
  output [31:0] PC_After
);

  wire and_1_out, and_2_out, and_3_out, and_4_out, and_5_out, beq, bgtz, blez, bltz, bne, Branch_Jump,
       comparator_1_eq, comparator_1_lt, comparator_2_gt, comparator_3_lt, j, jr, nop, not_1_out, or_1_out;
  wire [1:0] Jump_Type, Jump_Type_t;
  wire [31:0] bit_extender_1_out, Branch, multiplier_1_out, PC___4;
  wire [31:28] PC_Jump;

  Decoder_part #(.select(3)) decoder_1 (
    .out0(nop), .out1(beq), .out2(bne), .out3(blez), .out4(bgtz), .out5(bltz), .out6(j), .out7(jr),
    .sel(Instruction));  // open: en
  BitSelector #(.width(32), .group(4)) bitselector_1 (.in(PC_Before), .out(PC_Jump), .sel(3'b111));
  Comparator #(.width(32)) comparator_1 (
    .a(Rs), .b({32{1'b0}}), .eq(comparator_1_eq), .lt(comparator_1_lt));  // open: gt
  or or_1 (or_1_out, comparator_1_eq, comparator_1_lt);
  Comparator #(.width(32)) comparator_2 (.a(Rs), .b({32{1'b0}}), .gt(comparator_2_gt));  // open: eq, lt
  Comparator #(.width(32)) comparator_3 (.a(Rs), .b({32{1'b0}}), .lt(comparator_3_lt));  // open: gt, eq
  and and_1 (and_1_out, Rs______Rt, beq);
  not not_1 (not_1_out, Rs______Rt);
  and and_2 (and_2_out, not_1_out, bne);
  and and_3 (and_3_out, or_1_out, blez);
  and and_4 (and_4_out, comparator_2_gt, bgtz);
  and and_5 (and_5_out, comparator_3_lt, bltz);
  or or_2 (Branch_Jump, and_1_out, and_2_out, and_3_out, and_4_out, and_5_out);
  Multiplexer #(.select(2), .width(32)) multiplexer_1 (
    .in0(PC___4), .in1(Branch), .in2({PC_Jump, IA, 2'b00}), .in3(Rs), .out(PC_After), .sel(Jump_Type));  // open: en
  assign bit_extender_1_out = {{16{1'b0}}, k};  // Bit_Extender bit_extender_1
  Multiplier #(.width(32)) multiplier_1 (.a(bit_extender_1_out), .b(32'h4), .out(multiplier_1_out));  // open: cin, cout
  Priority_Encoder #(.select(2)) priority_encoder_1 (
    .in0(1'b1), .in1(Branch_Jump), .in2(j), .in3(jr), .out(Jump_Type_t));  // open: gs, en_out, en_in
  Adder #(.width(32)) adder_1 (.a(PC_Before), .b(32'h4), .out(PC___4));  // open: cin, cout
  Adder #(.width(32)) adder_2 (.a(PC___4), .b(multiplier_1_out), .out(Branch));  // open: cin, cout

  // Other names for the same wires on the sheet: PC_Jump[27:2] = IA
endmodule

module Register_File (
  input  [31:0] DI,
  input  [31:0] HighI,
  input  [31:0] LowI,
  input  [4:0] DA,
  input  Clock,
  input  Reset,
  input  pop_push,
  input  Stack,
  input  [4:0] SA,
  input  RW,
  input  HL_En,
  input  [4:0] SB,
  output [31:0] A,
  output [31:0] B,
  output [31:0] HighO,
  output [31:0] LowO,
  output [31:0] SP
);

  wire L0, L1, L2, L3, L4, L5, L6, L7, L8, L9, L10, L11, L12, L13, L14, L15, L16, L17, L18, L19, L20, L21,
       L22, L23, L24, L25, L26, L27, L28, L29, L30, L31, or_1_out;
  wire [31:0] adder_1_out, multiplexer_1_out, multiplexer_2_out, Q0, Q1, Q2, Q3, Q4, Q5, Q6, Q7, Q8, Q9, Q10,
       Q11, Q12, Q13, Q14, Q15, Q16, Q17, Q18, Q19, Q20, Q21, Q22, Q23, Q24, Q25, Q26, Q27, Q28, Q29, Q30,
       subtractor_1_out;

  Decoder_part #(.select(5), .disabled(0)) decoder_1 (
    .out0(L0), .out1(L1), .out2(L2), .out3(L3), .out4(L4), .out5(L5), .out6(L6), .out7(L7), .out8(L8),
    .out9(L9), .out10(L10), .out11(L11), .out12(L12), .out13(L13), .out14(L14), .out15(L15), .out16(L16),
    .out17(L17), .out18(L18), .out19(L19), .out20(L20), .out21(L21), .out22(L22), .out23(L23), .out24(L24),
    .out25(L25), .out26(L26), .out27(L27), .out28(L28), .out29(L29), .out30(L30), .out31(L31), .sel(DA),
    .en(RW));
  Register #(.width(32)) R0 (.Q(Q0));  // open: D, en, clk, clr
  Register #(.width(32)) R1 (.D(DI), .en(L1), .Q(Q1), .clk(Clock), .clr(Reset));
  Register #(.width(32)) R2 (.D(DI), .en(L2), .Q(Q2), .clk(Clock), .clr(Reset));
  Register #(.width(32)) R3 (.D(DI), .en(L3), .Q(Q3), .clk(Clock), .clr(Reset));
  Register #(.width(32)) R4 (.D(DI), .en(L4), .Q(Q4), .clk(Clock), .clr(Reset));
  Register #(.width(32)) R5 (.D(DI), .en(L5), .Q(Q5), .clk(Clock), .clr(Reset));
  Register #(.width(32)) R6 (.D(DI), .en(L6), .Q(Q6), .clk(Clock), .clr(Reset));
  Register #(.width(32)) R7 (.D(DI), .en(L7), .Q(Q7), .clk(Clock), .clr(Reset));
  Register #(.width(32)) HighR (.D(HighI), .en(HL_En), .Q(HighO), .clk(Clock), .clr(Reset));
  Subtractor #(.width(32)) subtractor_1 (.a(SP), .b(32'h4), .out(subtractor_1_out));  // open: bin, bout
  Adder #(.width(32)) adder_1 (.a(SP), .b(32'h4), .out(adder_1_out));  // open: cin, cout
  Register #(.width(32)) R8 (.D(DI), .en(L8), .Q(Q8), .clk(Clock), .clr(Reset));
  Register #(.width(32)) R9 (.D(DI), .en(L9), .Q(Q9), .clk(Clock), .clr(Reset));
  Register #(.width(32)) R10 (.D(DI), .en(L10), .Q(Q10), .clk(Clock), .clr(Reset));
  Register #(.width(32)) R11 (.D(DI), .en(L11), .Q(Q11), .clk(Clock), .clr(Reset));
  Register #(.width(32)) R12 (.D(DI), .en(L12), .Q(Q12), .clk(Clock), .clr(Reset));
  Register #(.width(32)) R13 (.D(DI), .en(L13), .Q(Q13), .clk(Clock), .clr(Reset));
  Register #(.width(32)) R14 (.D(DI), .en(L14), .Q(Q14), .clk(Clock), .clr(Reset));
  Register #(.width(32)) R15 (.D(DI), .en(L15), .Q(Q15), .clk(Clock), .clr(Reset));
  Multiplexer #(.width(32)) multiplexer_1 (
    .in0(subtractor_1_out), .in1(adder_1_out), .out(multiplexer_1_out), .sel(pop_push));  // open: en
  Multiplexer #(.width(32)) multiplexer_2 (
    .in0(DI), .in1(multiplexer_1_out), .out(multiplexer_2_out), .sel(Stack));  // open: en
  Register #(.width(32)) R16 (.D(DI), .en(L16), .Q(Q16), .clk(Clock), .clr(Reset));
  Register #(.width(32)) R17 (.D(DI), .en(L17), .Q(Q17), .clk(Clock), .clr(Reset));
  Register #(.width(32)) R18 (.D(DI), .en(L18), .Q(Q18), .clk(Clock), .clr(Reset));
  Register #(.width(32)) R19 (.D(DI), .en(L19), .Q(Q19), .clk(Clock), .clr(Reset));
  Register #(.width(32)) R20 (.D(DI), .en(L20), .Q(Q20), .clk(Clock), .clr(Reset));
  Register #(.width(32)) R21 (.D(DI), .en(L21), .Q(Q21), .clk(Clock), .clr(Reset));
  Register #(.width(32)) R22 (.D(DI), .en(L22), .Q(Q22), .clk(Clock), .clr(Reset));
  Register #(.width(32)) R23 (.D(DI), .en(L23), .Q(Q23), .clk(Clock), .clr(Reset));
  or or_1 (or_1_out, L31, Stack);
  Register #(.width(32)) LowR (.D(LowI), .en(HL_En), .Q(LowO), .clk(Clock), .clr(Reset));
  Register #(.width(32)) R31 (.D(multiplexer_2_out), .en(or_1_out), .Q(SP), .clk(Clock), .clr(Reset));
  Register #(.width(32)) R24 (.D(DI), .en(L24), .Q(Q24), .clk(Clock), .clr(Reset));
  Register #(.width(32)) R25 (.D(DI), .en(L25), .Q(Q25), .clk(Clock), .clr(Reset));
  Register #(.width(32)) R26 (.D(DI), .en(L26), .Q(Q26), .clk(Clock), .clr(Reset));
  Register #(.width(32)) R27 (.D(DI), .en(L27), .Q(Q27), .clk(Clock), .clr(Reset));
  Register #(.width(32)) R28 (.D(DI), .en(L28), .Q(Q28), .clk(Clock), .clr(Reset));
  Register #(.width(32)) R29 (.D(DI), .en(L29), .Q(Q29), .clk(Clock), .clr(Reset));
  Register #(.width(32)) R30 (.D(DI), .en(L30), .Q(Q30), .clk(Clock), .clr(Reset));
  Multiplexer #(.select(5), .width(32)) multiplexer_3 (
    .in0(Q0), .in1(Q1), .in2(Q2), .in3(Q3), .in4(Q4), .in5(Q5), .in6(Q6), .in7(Q7), .in8(Q8), .in9(Q9),
    .in10(Q10), .in11(Q11), .in12(Q12), .in13(Q13), .in14(Q14), .in15(Q15), .in16(Q16), .in17(Q17),
    .in18(Q18), .in19(Q19), .in20(Q20), .in21(Q21), .in22(Q22), .in23(Q23), .in24(Q24), .in25(Q25),
    .in26(Q26), .in27(Q27), .in28(Q28), .in29(Q29), .in30(Q30), .in31(SP), .out(A), .sel(SA));  // open: en
  Multiplexer #(.select(5), .width(32)) multiplexer_4 (
    .in0(Q0), .in1(Q1), .in2(Q2), .in3(Q3), .in4(Q4), .in5(Q5), .in6(Q6), .in7(Q7), .in8(Q8), .in9(Q9),
    .in10(Q10), .in11(Q11), .in12(Q12), .in13(Q13), .in14(Q14), .in15(Q15), .in16(Q16), .in17(Q17),
    .in18(Q18), .in19(Q19), .in20(Q20), .in21(Q21), .in22(Q22), .in23(Q23), .in24(Q24), .in25(Q25),
    .in26(Q26), .in27(Q27), .in28(Q28), .in29(Q29), .in30(Q30), .in31(SP), .out(B), .sel(SB));  // open: en

  // Other names for the same wires on the sheet: Q31[31:0] = SP
endmodule

module Decoder (
  input  [5:0] in_1,
  input  [5:0] in_2,
  output [1:0] Special_Op_Out,
  output RAM_load,
  output pop,
  output comp,
  output Hi_Read,
  output [2:0] out_8,
  output HL,
  output \unsigned ,
  output [2:0] Branch_Op_Out,
  output [2:0] ALU_Op_Out
);

  wire add, addi, ALU_Op, \and , andi, beq, bgtz, blez, bltz, bne, Branch_Op, comparator_17_eq,
       comparator_18_eq, comparator_19_eq, comparator_20_eq, comparator_21_eq, comparator_22_eq,
       comparator_23_eq, comparator_24_eq, comparator_25_eq, comparator_26_eq, comparator_27_eq,
       comparator_28_eq, comparator_29_eq, comparator_30_eq, comparator_31_eq, comparator_32_eq,
       comparator_33_eq, comparator_34_eq, comparator_35_eq, comparator_36_eq, comparator_37_eq,
       comparator_38_eq, comparator_39_eq, comparator_40_eq, div, divu, halt, Inmediate_Op, jr, jump, kbd,
       mflo, mult, mulu, nop, \nor , O_one, O_zero, \or , or_8_out, or_9_out, or_11_out, or_12_out,
       or_13_out, or_14_out, or_16_out, or_17_out, or_18_out, ori, priority_encoder_3_gs, push, RAM_Op,
       Register_Op, rnd, slt, slti, sltiu, sltu, Special_Op, Stack_Op, sub, sw, tty, \xor , xori;
  wire [2:0] priority_encoder_3_out;

  Comparator #(.width(6), .mode("unsigned")) comparator_1 (.a(in_1), .b(6'b001010), .eq(slti));  // open: gt, lt
  Comparator #(.width(6), .mode("unsigned")) comparator_2 (.a(in_1), .b(6'b001011), .eq(sltiu));  // open: gt, lt
  Comparator #(.width(6), .mode("unsigned")) comparator_3 (.a(in_1), .b(6'b000100), .eq(beq));  // open: gt, lt
  Comparator #(.width(6), .mode("unsigned")) comparator_4 (.a(in_1), .b(6'b000101), .eq(bne));  // open: gt, lt
  Comparator #(.width(6), .mode("unsigned")) comparator_5 (.a(in_1), .b(6'b000110), .eq(blez));  // open: gt, lt
  Comparator #(.width(6), .mode("unsigned")) comparator_6 (.a(in_1), .b(6'b000111), .eq(bgtz));  // open: gt, lt
  Comparator #(.width(6), .mode("unsigned")) comparator_7 (.a(in_1), .b(6'b000001), .eq(bltz));  // open: gt, lt
  or or_1 (Stack_Op, pop, push);
  Comparator #(.width(6), .mode("unsigned")) comparator_8 (.a(in_1), .b(6'b001000), .eq(addi));  // open: gt, lt
  Comparator #(.width(6), .mode("unsigned")) comparator_9 (.a(in_1), .b(6'b000010), .eq(jump));  // open: gt, lt
  Comparator #(.width(6), .mode("unsigned")) comparator_10 (.a(in_1), .b(6'b001100), .eq(andi));  // open: gt, lt
  Comparator #(.width(6), .mode("unsigned")) comparator_11 (.a(in_1), .b(6'b001101), .eq(ori));  // open: gt, lt
  Comparator #(.width(6), .mode("unsigned")) comparator_12 (.a(in_1), .b(6'b001110), .eq(xori));  // open: gt, lt
  Comparator #(.width(6), .mode("unsigned")) comparator_13 (.a(in_1), .b(6'b100011), .eq(RAM_load));  // open: gt, lt
  Comparator #(.width(6), .mode("unsigned")) comparator_14 (.a(in_1), .b(6'b101011), .eq(sw));  // open: gt, lt
  Comparator #(.width(6), .mode("unsigned")) comparator_15 (.a(in_1), .b({6{1'b0}}), .eq(O_zero));  // open: gt, lt
  Comparator #(.width(6), .mode("unsigned")) comparator_16 (.a(in_1), .b({6{1'b1}}), .eq(O_one));  // open: gt, lt
  or or_2 (RAM_Op, RAM_load, sw);
  or or_3 (Register_Op, Hi_Read, mflo);
  Comparator #(.width(6), .mode("unsigned")) comparator_17 (
    .a(in_2), .b(6'b100000), .eq(comparator_17_eq));  // open: gt, lt
  Comparator #(.width(6), .mode("unsigned")) comparator_18 (
    .a(in_2), .b(6'b100010), .eq(comparator_18_eq));  // open: gt, lt
  Comparator #(.width(6), .mode("unsigned")) comparator_19 (
    .a(in_2), .b(6'b011000), .eq(comparator_19_eq));  // open: gt, lt
  Comparator #(.width(6), .mode("unsigned")) comparator_20 (
    .a(in_2), .b(6'b011001), .eq(comparator_20_eq));  // open: gt, lt
  Comparator #(.width(6), .mode("unsigned")) comparator_21 (
    .a(in_2), .b(6'b011010), .eq(comparator_21_eq));  // open: gt, lt
  Comparator #(.width(6), .mode("unsigned")) comparator_22 (
    .a(in_2), .b(6'b011011), .eq(comparator_22_eq));  // open: gt, lt
  and and_1 (add, comparator_17_eq, O_zero);
  and and_2 (sub, comparator_18_eq, O_zero);
  and and_3 (mult, comparator_19_eq, O_zero);
  and and_4 (mulu, comparator_20_eq, O_zero);
  and and_5 (div, comparator_21_eq, O_zero);
  and and_6 (divu, comparator_22_eq, O_zero);
  or or_4 (ALU_Op, add, sub, mult, mulu, div, divu, \and , \or , \xor , \nor , slt, sltu);
  Comparator #(.width(6), .mode("unsigned")) comparator_23 (
    .a(in_2), .b(6'b100100), .eq(comparator_23_eq));  // open: gt, lt
  Comparator #(.width(6), .mode("unsigned")) comparator_24 (
    .a(in_2), .b(6'b100101), .eq(comparator_24_eq));  // open: gt, lt
  Comparator #(.width(6), .mode("unsigned")) comparator_25 (
    .a(in_2), .b(6'b100111), .eq(comparator_25_eq));  // open: gt, lt
  Comparator #(.width(6), .mode("unsigned")) comparator_26 (
    .a(in_2), .b(6'b101000), .eq(comparator_26_eq));  // open: gt, lt
  Comparator #(.width(6), .mode("unsigned")) comparator_27 (
    .a(in_2), .b(6'b101010), .eq(comparator_27_eq));  // open: gt, lt
  Comparator #(.width(6), .mode("unsigned")) comparator_28 (
    .a(in_2), .b(6'b101011), .eq(comparator_28_eq));  // open: gt, lt
  and and_7 (\and , comparator_23_eq, O_zero);
  and and_8 (\or , comparator_24_eq, O_zero);
  and and_9 (\nor , comparator_25_eq, O_zero);
  and and_10 (\xor , comparator_26_eq, O_zero);
  and and_11 (slt, comparator_27_eq, O_zero);
  and and_12 (sltu, comparator_28_eq, O_zero);
  or or_5 (Inmediate_Op, andi, ori, xori, addi, slti, sltiu);
  Comparator #(.width(6), .mode("unsigned")) comparator_29 (
    .a(in_2), .b(6'b010000), .eq(comparator_29_eq));  // open: gt, lt
  Comparator #(.width(6), .mode("unsigned")) comparator_30 (
    .a(in_2), .b(6'b010010), .eq(comparator_30_eq));  // open: gt, lt
  Comparator #(.width(6), .mode("unsigned")) comparator_31 (
    .a(in_2), .b({6{1'b0}}), .eq(comparator_31_eq));  // open: gt, lt
  Comparator #(.width(6), .mode("unsigned")) comparator_32 (
    .a(in_2), .b(6'b001000), .eq(comparator_32_eq));  // open: gt, lt
  and and_13 (Hi_Read, comparator_29_eq, O_zero);
  and and_14 (mflo, comparator_30_eq, O_zero);
  and and_15 (nop, comparator_31_eq, O_zero);
  and and_16 (jr, comparator_32_eq, O_zero);
  or or_6 (Branch_Op, beq, jump, bne, jr, blez, nop, bgtz, bltz);
  or or_7 (Special_Op, halt, tty, rnd, kbd);
  Comparator #(.width(6), .mode("unsigned")) comparator_33 (
    .a(in_1), .b(6'b111000), .eq(comparator_33_eq));  // open: gt, lt
  Comparator #(.width(6), .mode("unsigned")) comparator_34 (
    .a(in_2), .b({6{1'b0}}), .eq(comparator_34_eq));  // open: gt, lt
  Comparator #(.width(6), .mode("unsigned")) comparator_35 (
    .a(in_1), .b(6'b111000), .eq(comparator_35_eq));  // open: gt, lt
  Comparator #(.width(6), .mode("unsigned")) comparator_36 (
    .a(in_2), .b(6'b000001), .eq(comparator_36_eq));  // open: gt, lt
  Comparator #(.width(6), .mode("unsigned")) comparator_37 (
    .a(in_2), .b({6{1'b1}}), .eq(comparator_37_eq));  // open: gt, lt
  Comparator #(.width(6), .mode("unsigned")) comparator_38 (
    .a(in_2), .b(6'b000001), .eq(comparator_38_eq));  // open: gt, lt
  Comparator #(.width(6), .mode("unsigned")) comparator_39 (
    .a(in_2), .b(6'b000010), .eq(comparator_39_eq));  // open: gt, lt
  Comparator #(.width(6), .mode("unsigned")) comparator_40 (
    .a(in_2), .b(6'b000100), .eq(comparator_40_eq));  // open: gt, lt
  Priority_Encoder priority_encoder_1 (
    .in0(Branch_Op), .in1(ALU_Op), .in2(Inmediate_Op), .in3(Register_Op), .in4(RAM_Op), .in5(Stack_Op),
    .in6(Special_Op), .out(out_8), .en_in(1'b1));  // open: in7, gs, en_out
  and and_17 (pop, comparator_33_eq, comparator_34_eq);
  and and_18 (push, comparator_35_eq, comparator_36_eq);
  and and_19 (halt, comparator_37_eq, O_one);
  and and_20 (tty, comparator_38_eq, O_one);
  and and_21 (rnd, comparator_39_eq, O_one);
  and and_22 (kbd, comparator_40_eq, O_one);
  or or_8 (or_8_out, div, divu);
  or or_9 (or_9_out, \xor , xori);
  or or_10 (\unsigned , mulu, divu, sltu, sltiu);
  or or_11 (or_11_out, mult, mulu);
  or or_12 (or_12_out, div, divu);
  or or_13 (or_13_out, mult, mulu);
  or or_14 (or_14_out, \and , andi);
  Priority_Encoder #(.disabled(0)) priority_encoder_2 (
    .in0(nop), .in1(beq), .in2(bne), .in3(blez), .in4(bgtz), .in5(bltz), .in6(jump), .in7(jr),
    .out(Branch_Op_Out), .en_in(Branch_Op));  // open: gs, en_out
  or or_15 (HL, or_11_out, or_12_out);
  or or_16 (or_16_out, \or , ori);
  or or_17 (or_17_out, add, addi);
  Priority_Encoder #(.disabled(0)) priority_encoder_3 (
    .in0(or_17_out), .in1(sub), .in2(or_13_out), .in3(or_8_out), .in4(or_14_out), .in5(\nor ),
    .in6(or_16_out), .in7(or_9_out), .out(priority_encoder_3_out), .en_in(or_18_out),
    .gs(priority_encoder_3_gs), .en_out(comp));
  or or_18 (or_18_out, ALU_Op, Inmediate_Op);
  Multiplexer #(.width(3)) multiplexer_1 (
    .in0(3'b000), .in1(priority_encoder_3_out), .out(ALU_Op_Out), .sel(priority_encoder_3_gs));  // open: en
  Priority_Encoder #(.select(2), .disabled(0)) priority_encoder_4 (
    .in0(halt), .in1(tty), .in2(rnd), .in3(kbd), .out(Special_Op_Out), .en_in(Special_Op));  // open: gs, en_out

  // Other names for the same wires on the sheet: algo_ahi[2:0] = out_8; Comparation = comp; Func_code[5:0] = in_2;
  //   lw = RAM_load; mfhi = Hi_Read; OP_code[5:0] = in_1
endmodule

module Control_Unit (
  input  [5:0] OP_code,
  input  [5:0] Func_code,
  input  [3:0] Write_Time,
  input  [3:0] Read_Time,
  input  Start,
  input  CLK,
  input  RST,
  output [2:0] ALU_Op,
  output [2:0] Branch_Op,
  output Inmediate,
  output Unsigned,
  output Comparation,
  output Hi_Lo_EN,
  output Register_Op,
  output Hi_Lo_Selector,
  output RAM_op,
  output Stack_op,
  output pop_push,
  output SP_En,
  output RND,
  output KBD_Sel,
  output Chip_selector,
  output Load_Instruction,
  output Read_Write,
  output Load_PC,
  output RAM_RW,
  output TTY,
  output KBD_ENABLE,
  output END
);

  wire CS_1, CS_2, CS_3, CS_4, CS_5, d_ff_1_q, demultiplexer_1_out0, demultiplexer_1_out1,
       demultiplexer_2_out0, demultiplexer_3_out0, demultiplexer_3_out4, demultiplexer_3_out5,
       demultiplexer_3_out6, demultiplexer_4_out0, demultiplexer_4_out1, demultiplexer_5_out1,
       demultiplexer_6_out0, demultiplexer_7_out0, demultiplexer_7_out1, demultiplexer_8_out0,
       demultiplexer_9_out0, demultiplexer_9_out1, demultiplexer_10_out0, IDLE_qn, loaded, lw, OP___Func_q,
       or_1_out, or_2_out, or_3_out, or_4_out, or_5_out, or_6_out, or_7_out, or_8_out, or_9_out, or_10_out,
       pop, R_W_1, R_W_4, RESET_q, SP_1, started, WAIT_2_q;
  wire [1:0] Spec_op;
  wire [2:0] Inst_Type;
  wire [3:0] counter_1_q, Load_Time;

  Decoder decoder_1 (
    .in_1(OP_code), .in_2(Func_code), .RAM_load(lw), .comp(Comparation), .Hi_Read(Hi_Lo_Selector),
    .out_8(Inst_Type), .HL(Hi_Lo_EN), .\unsigned (Unsigned), .Branch_Op_Out(Branch_Op), .ALU_Op_Out(ALU_Op),
    .Special_Op_Out(Spec_op), .pop(pop));
  D_Flip_Flop IDLE (.clk(CLK), .D(demultiplexer_1_out0), .Qn(IDLE_qn), .reset(RST));  // open: Q, preset, en
  or or_1 (or_1_out, IDLE_qn, RESET_q);
  Demultiplexer #(.disabled(0)) demultiplexer_1 (
    .out0(demultiplexer_1_out0), .out1(demultiplexer_1_out1), .in(or_1_out), .sel(Start), .en(started));
  or or_2 (or_2_out, demultiplexer_2_out0, demultiplexer_1_out1);
  D_Flip_Flop LOADING (.clk(CLK), .D(or_2_out), .Q(CS_1), .reset(or_3_out));  // open: Qn, preset, en
  Demultiplexer #(.enable("false")) demultiplexer_2 (
    .out0(demultiplexer_2_out0), .out1(Load_Instruction), .in(CS_1), .sel(loaded));
  or or_3 (or_3_out, ~started, RST);  // OR_Gate
  D_Flip_Flop OP___Func (.clk(CLK), .D(Load_Instruction), .Q(OP___Func_q), .reset(RST));  // open: Qn, preset, en
  Demultiplexer #(.select(3)) demultiplexer_3 (
    .out0(demultiplexer_3_out0), .out1(R_W_1), .out2(Inmediate), .out3(Register_Op),
    .out4(demultiplexer_3_out4), .out5(demultiplexer_3_out5), .out6(demultiplexer_3_out6), .in(OP___Func_q),
    .sel(Inst_Type));  // open: out7, en
  Demultiplexer #(.enable("false")) demultiplexer_4 (
    .out0(demultiplexer_4_out0), .out1(demultiplexer_4_out1), .in(demultiplexer_3_out4), .sel(lw));
  Demultiplexer #(.enable("false")) demultiplexer_5 (
    .out0(SP_1), .out1(demultiplexer_5_out1), .in(demultiplexer_3_out5), .sel(pop));
  Demultiplexer #(.select(2), .enable("false")) demultiplexer_6 (
    .out0(demultiplexer_6_out0), .out1(TTY), .out2(RND), .out3(KBD_Sel), .in(demultiplexer_3_out6),
    .sel(Spec_op));
  or or_4 (or_4_out, END, demultiplexer_6_out0);
  Counter #(.width(4), .max('hf)) counter_1 (
    .count(Chip_selector), .Q(counter_1_q), .clk(CLK), .clr(d_ff_1_q));  // open: load, D, carry
  or or_5 (or_5_out, demultiplexer_7_out0, demultiplexer_4_out0);
  or or_6 (or_6_out, demultiplexer_8_out0, demultiplexer_4_out1);
  or or_7 (or_7_out, demultiplexer_9_out0, SP_1);
  or or_8 (or_8_out, demultiplexer_10_out0, demultiplexer_5_out1);
  D_Flip_Flop HALT (.clk(CLK), .D(or_4_out), .Q(END), .reset(RST));  // open: Qn, preset, en
  D_Flip_Flop LOADING_2 (.clk(CLK), .D(or_5_out), .Q(CS_2), .reset(RST));  // open: Qn, preset, en
  D_Flip_Flop LOADING_3 (.clk(CLK), .D(or_6_out), .Q(CS_3), .reset(RST));  // open: Qn, preset, en
  D_Flip_Flop LOADING_4 (.clk(CLK), .D(or_7_out), .Q(CS_4), .reset(RST));  // open: Qn, preset, en
  D_Flip_Flop LOADING_5 (.clk(CLK), .D(or_8_out), .Q(CS_5), .reset(RST));  // open: Qn, preset, en
  Comparator #(.width(4), .mode("unsigned")) comparator_1 (
    .a(counter_1_q), .b(Load_Time), .eq(loaded));  // open: gt, lt
  D_Flip_Flop WAIT (.clk(CLK), .D(KBD_Sel), .Q(KBD_ENABLE), .reset(RST));  // open: Qn, preset, en
  D_Flip_Flop d_ff_1 (.clk(CLK), .D(loaded), .Q(d_ff_1_q), .reset(RST));  // open: Qn, preset, en
  Demultiplexer #(.enable("false")) demultiplexer_7 (
    .out0(demultiplexer_7_out0), .out1(demultiplexer_7_out1), .in(CS_2), .sel(loaded));
  Demultiplexer #(.enable("false")) demultiplexer_8 (
    .out0(demultiplexer_8_out0), .out1(R_W_4), .in(CS_3), .sel(loaded));
  Demultiplexer #(.enable("false")) demultiplexer_9 (
    .out0(demultiplexer_9_out0), .out1(demultiplexer_9_out1), .in(CS_4), .sel(loaded));
  Demultiplexer #(.enable("false")) demultiplexer_10 (
    .out0(demultiplexer_10_out0), .out1(pop_push), .in(CS_5), .sel(loaded));
  D_Flip_Flop WAIT_2 (.clk(CLK), .D(TTY), .Q(WAIT_2_q), .reset(RST));  // open: Qn, preset, en
  or or_9 (or_9_out, Load_PC, RST);
  D_Flip_Flop u_STARTED (
    .clk(CLK), .D(Load_Instruction), .Qn(started), .en(started), .reset(or_9_out));  // open: Q, preset
  or or_10 (or_10_out, demultiplexer_3_out0, R_W_1, Inmediate, Register_Op, demultiplexer_7_out1, R_W_4, demultiplexer_9_out1, pop_push, WAIT_2_q, RND, KBD_ENABLE);
  D_Flip_Flop u_END (.clk(CLK), .D(or_10_out), .Q(Load_PC), .reset(RST));  // open: Qn, preset, en
  D_Flip_Flop RESET (.clk(CLK), .D(Load_PC), .Q(RESET_q), .reset(RST));  // open: Qn, preset, en
  Multiplexer #(.width(4), .enable("false")) multiplexer_1 (
    .in0(Read_Time), .in1(Write_Time), .out(Load_Time), .sel(RAM_RW));
  or or_11 (RAM_RW, CS_2, CS_4);
  or or_12 (RAM_op, CS_2, CS_3);
  or or_13 (Stack_op, CS_4, CS_5);
  or or_14 (SP_En, SP_1, pop_push);
  or or_15 (Read_Write, R_W_1, Inmediate, Register_Op, R_W_4, pop_push, RND, KBD_Sel);
  or or_16 (Chip_selector, CS_1, CS_2, CS_3, CS_4, CS_5);

  // Other names for the same wires on the sheet: Comp = Comparation; CS = Chip_selector; Hi_read = Hi_Lo_Selector;
  //   HL = Hi_Lo_EN; KBD_En = KBD_ENABLE; LI = Load_Instruction; PC = Load_PC; pop_S = pop_push; R_W_5 = pop_push;
  //   SP_2 = pop_push; R_W = Read_Write; R_W_2 = Inmediate; R_W_6 = RND; R_W_7 = KBD_Sel; RAM_op_1 = CS_2;
  //   RAM_RW_1 = CS_2; RAM_op_2 = CS_3; R_W_3 = Register_Op; Reg_Op = Register_Op; RT[3:0] = Read_Time; SP = SP_En;
  //   RAM_RW_2 = CS_4; Stack_op_1 = CS_4; Stack_op_2 = CS_5; uns = Unsigned; WT[3:0] = Write_Time
endmodule

module Little_Endian (
  input  [31:0] in_1,
  output [31:0] Output
);


  assign Output = {in_1[7:0], in_1[15:8], in_1[23:16], in_1[31:24]};
endmodule
